# Fritzing sketch Untitled Sketch 2 (saved by Fritzing 0.8.7b)
breadboards: 1

parts:
  Part1 = Arduino Uno (Rev3)
  LED1 = LED - 5mm [color="Red (633nm)" package="5 mm [THT]"]
  R1 = Resistor [tolerance=±5% resistance=220 package=THT]
  S1 = Pushbutton [package="[SMD]"]
  R2 = Resistor [tolerance=±5% resistance=220 package=THT]
  S2 = Pushbutton [package="[SMD]"]
  R3 = Resistor [tolerance=±5% resistance=220 package=THT]
  R4 = Trimmer Potentiometer [maximum_resistance=10kΩ package=THT]  # not connected
  U1 = LCD-16X2 [package=lcd-16x2]

nets:
  N1: Part1.D8, S1.Pin_3, S1.Pin_4, R2.Pin_0
  N2: Part1.D9_PWM, R1.Pin_1
  N3: Part1.D10_PWM/SS, S2.Pin_3, S2.Pin_4, R3.Pin_0
  N4: Part1.D1/TX, U1.RS
  N5: Part1.D2, U1.E
  N6: Part1.D4, U1.DB4
  N7: Part1.D5_PWM, U1.DB5
  N8: Part1.D6_PWM, U1.DB6
  N9: Part1.D7, U1.DB7
  5V: Part1.5V, S1.Pin_1, S1.Pin_2, S2.Pin_1, S2.Pin_2, U1.VDD, U1.A
  GND: Part1.GND, LED1.cathode, R2.Pin_1, U1.VSS, U1.R_W, U1.K
  N10: LED1.anode, R1.Pin_0
